# Fritzing sketch Circuit Diagram (saved by Fritzing 0.9.3b)
breadboards: 1

parts:
  Part1 = Arduino Nano (Rev3.0)
  R1 = Resistor [tolerance=±5% resistance=10k package=THT]
  R2 = Photocell (LDR) [package=THT]
  Part2 = Soil Moisture Sensor
  RHT1 = Humidity and Temperature Sensor RHT03
  U1 = LCD-16X2 [package=lcd-16x2_noholes]  # not connected
  LCM1602_IIC2 = LCM1602 IIC [part_number="LCM1602 IIC" chip_label="LCM1602 IIC" package="DIP (Dual Inline) [THT]"]
  M1 = 1 chan 5v relay module
  R3 = Resistor [tolerance=±5% resistance=10k package=THT]
  M2 = DC Motor  # not connected
  R4 = Resistor [tolerance=±5% resistance=10k package=THT]
  R5 = Resistor [tolerance=±5% resistance=10k package=THT]
  LED1 = RGB LED (com. cathode, rbg) [package="5 mm [THT]"]

nets:
  GND: Part1.GND, R1.Pin_1, Part2.GND, RHT1.GND_2, LCM1602_IIC2.GND, M1.pin_2, LED1.common_cathode
  N1: Part1.D8, RHT1.Data-signal
  N2: Part1.D10, M1.pin_3
  N3: Part1.D11/MOSI, R4.Pin_0
  N4: Part1.D12/MISO, R5.Pin_1
  VCC: Part1.5V, R2.pin_1, Part2.VCC, RHT1.Vcc, LCM1602_IIC2.VCC, R3.Pin_1
  N5: Part1.A5, LCM1602_IIC2.SCL
  N6: Part1.A4, LCM1602_IIC2.SDA
  N7: Part1.A1, Part2.SIG
  N8: Part1.A0, R1.Pin_0, R2.pin_0
  N9: M1.pin_1, R3.Pin_0
  N10: R4.Pin_1, LED1.green_anode
  N11: R5.Pin_0, LED1.red_anode

custom parts:
  LCM1602 IIC: I2C-Module to use a 1602 or 2004 LCD on with the wire.h libory Serial LCD Modul
  1 chan 5v relay module: 1 Channel 5V Relay Module Board Shield with Optocoupler Support High and Low Level Trigger for Arduino.
